// Logisim project CustomAdder.circ as structural Verilog: 1 circuit, main circuit CustomAdder
module CustomAdder (
  input  [7:0] FirstOperand,
  input  [7:0] SecondOperand,
  output [7:0] Result
);

  Adder adder_1 (.a(FirstOperand), .b(SecondOperand), .out(Result));  // open: cin, cout

  // Other names for the same wires on the sheet: A[7:0] = FirstOperand; B[7:0] = SecondOperand; C[7:0] = Result
endmodule
