// Logisim project CustomMultiplier.circ as structural Verilog: 1 circuit, main circuit CustomMultiplier
module CustomMultiplier (
  input  [7:0] FirstOperand,
  input  [7:0] SecondOperand,
  input  Clock,
  input  in_4,
  input  in_5,
  input  in_6,
  output [7:0] Result,
  output Done
);

  wire d_ff_1_qn, nor_1_out, or_1_out, or_2_out, shift_register_1_p1, shift_register_1_p3,
       shift_register_1_p14, shift_register_1_p15, shift_register_1_p16, shift_register_2_p18,
       shift_register_2_p19, shift_register_2_p20, shift_register_2_p21, shift_register_2_p22,
       shift_register_2_p23, shift_register_2_p24, shift_register_2_p25, shift_register_2_p26,
       shift_register_2_p27, shift_register_2_p28, shift_register_2_p29, shift_register_2_p30, Start;
  wire [7:0] adder_1_out, and_1_out;

  D_Flip_Flop d_ff_1 (.D(in_4), .clk(Clock), .Q(Start), .Qn(d_ff_1_qn));  // open: preset, reset
  // Shift_Register shift_register_1: pin names not known; wires that end beside it: shift_register_1_p1, shift_register_1_p1, shift_register_1_p3, shift_register_1_p3, in_5, d_ff_1_qn, Start, Clock, in_5, SecondOperand[0], SecondOperand[1], SecondOperand[2], SecondOperand[3], shift_register_1_p14, shift_register_1_p15, shift_register_1_p16
  // Shift_Register shift_register_2: pin names not known; wires that end beside it: SecondOperand[4], SecondOperand[5], SecondOperand[6], SecondOperand[7], in_5, d_ff_1_qn, Start, Clock, in_5, FirstOperand[7], FirstOperand[6], FirstOperand[5], FirstOperand[4], FirstOperand[3], FirstOperand[2], FirstOperand[1], FirstOperand[0], shift_register_2_p18, shift_register_2_p19, shift_register_2_p20, shift_register_2_p21, shift_register_2_p22, shift_register_2_p23, shift_register_2_p24, shift_register_2_p25, shift_register_2_p26, shift_register_2_p27, shift_register_2_p28, shift_register_2_p29, shift_register_2_p30
  or or_1 (or_1_out, shift_register_2_p19, shift_register_2_p20, shift_register_2_p21, shift_register_2_p22, shift_register_2_p18, shift_register_1_p16, shift_register_1_p15, shift_register_1_p14);
  and and_1 (and_1_out[0], shift_register_1_p14, shift_register_2_p30);
  and and_2 (and_1_out[1], shift_register_1_p15, shift_register_2_p30);
  and and_3 (and_1_out[2], shift_register_1_p16, shift_register_2_p30);
  and and_4 (and_1_out[3], shift_register_2_p18, shift_register_2_p30);
  and and_5 (and_1_out[4], shift_register_2_p19, shift_register_2_p30);
  and and_6 (and_1_out[5], shift_register_2_p20, shift_register_2_p30);
  and and_7 (and_1_out[6], shift_register_2_p21, shift_register_2_p30);
  and and_8 (and_1_out[7], shift_register_2_p22, shift_register_2_p30);
  or or_2 (or_2_out, shift_register_2_p23, shift_register_2_p24, shift_register_2_p25, shift_register_2_p26, shift_register_2_p27, shift_register_2_p28, shift_register_2_p29, shift_register_2_p30);
  nor nor_1 (nor_1_out, or_1_out, or_2_out);
  Adder adder_1 (.a(Result), .b(and_1_out), .out(adder_1_out));  // open: cin, cout
  and and_9 (Done, nor_1_out, Start);
  Register register_1 (.D(adder_1_out), .en(in_6), .clk(Clock), .Q(Result));  // open: clr

  // Other names for the same wires on the sheet: A[7:0] = FirstOperand; B[7:0] = SecondOperand; C[7:0] = Result;
  //   clk = Clock
endmodule
